# Fritzing sketch doorlock (saved by Fritzing 0.9.3b)
breadboards: 1

parts:
  Parça1 = Arduino Uno (Rev3) - ICSP
  S1 = Momentary Switch [package=ksa_sealed_tac_switch]
  S2 = Momentary Switch [package=ksa_sealed_tac_switch]
  R4 = Resistor [tolerance=±5% resistance=220 package="2010 [SMD]"]
  R5 = Resistor [tolerance=±5% resistance=220 package="2010 [SMD]"]
  LED2 = smd LED [color="Red (633nm)" package="1206 [SMD]"]
  LED1 = smd LED [color="Green (570nm)" package="0805 [SMD]"]
  R6 = Resistor [tolerance=±5% resistance=220 package="0805 [SMD]"]
  R7 = Resistor [tolerance=±5% resistance=220 package="0805 [SMD]"]
  Parça2 = songle relay
  U1 = RFID RC522 SIP - 8 pins [chip_label="RFID RC522" package="SIP (Single Inline) [THT]"]
  J1 = Piezo Speaker

nets:
  N1: Parça1.D8, J1.pin2
  N2: Parça1.D9_PWM, U1.RST
  N3: Parça1.D10_PWM/SS, U1.SCA
  N4: Parça1.D11_PWM/MOSI, U1.MOSI
  N5: Parça1.D12/MISO, U1.MISO
  N6: Parça1.D13/SCK, U1.SCK
  GND: Parça1.GND, U1.GND
  N7: Parça1.D3_PWM, Parça2.VCC
  N8: Parça1.D4, S2.1, S2.2, R5.Pin_1
  N9: Parça1.D5_PWM, LED1.anode
  N10: Parça1.D6_PWM, S1.1, S1.2, R4.Pin_1
  N11: Parça1.D7, LED2.anode
  N12: Parça1.3V3, U1.3.3_V
  N13: S1.3, S1.4, S2.3, S2.4
  N14: R4.Pin_0, R5.Pin_0, R6.Pin_0, R7.Pin_0, Parça2.GND, J1.pin1
  N15: LED2.cathode, R6.Pin_1
  N16: LED1.cathode, R7.Pin_1

custom parts:
  RFID RC522 SIP - 8 pins: A SIP stand-in part for RFID RC522 . With 8 pins on a 300 mil single inline package (SIP) footprint.
